# Fritzing sketch test (saved by Fritzing 0.9.3b)
breadboards: 1

parts:
  Part1 = Arduino Nano (Rev3.0)
  M1 = DC Motor
  Part2 = Motor Driver 1A Dual TB6612FNG
  Part3 = Thumb Joystick

nets:
  GND: Part1.GND, Part2.GND, Part3.GND
  N1: Part1.D2, Part3.SEL
  N2: Part1.D7, Part2.AIN1
  N3: Part1.D8, Part2.AIN2
  N4: Part1.D9, Part2.PWMA
  6V: Part1.VIN, Part2.VM
  VCC: Part1.5V, Part2.VCC, Part2.STBY, Part3.VCC
  N5: Part1.A1, Part3.VERT
  N6: Part1.A0, Part3.HORZ
  N7: M1.pin_1, Part2.A01
  N8: M1.pin_2, Part2.A02

notes:
  TB6612FNG Test, 0.1
